# Fritzing sketch Breadboard_Circuit (saved by Fritzing 0.9.9b)
breadboards: 1

parts:
  IC1 = ULN2003A [package="SO16 [SMD]"]
  SM1 = 28BYJ-48 Stepper Motor [part_number=28BYJ-48]
  Part1 = Arduino Uno (Rev3)
  LED1 = smd LED [color="Red (633nm)" package="0805 [SMD]"]
  LED2 = smd LED [color="Red (633nm)" package="0805 [SMD]"]
  LED3 = smd LED [color="Red (633nm)" package="0805 [SMD]"]
  LED4 = smd LED [color="Red (633nm)" package="0805 [SMD]"]
  R1 = Resistor [tolerance=±0.5% resistance=1k package=THT]
  R2 = Resistor [tolerance=±0.5% resistance=1k package=THT]
  R3 = Resistor [tolerance=±0.5% resistance=1k package=THT]
  R4 = Resistor [tolerance=±0.5% resistance=1k package=THT]

nets:
  N1: IC1.In_1, Part1.D11_PWM/MOSI
  N2: IC1.In_2, Part1.D10_PWM/SS
  N3: IC1.In_3, Part1.D9_PWM
  N4: IC1.In_4, Part1.D8
  N5: IC1.0V, Part1.GND, LED1.anode, LED2.anode, LED3.anode, LED4.anode
  N6: IC1.COM_-_Common, SM1.red-pin, Part1.5V
  N7: IC1.Out_4, SM1.orange-pin, R1.Pin_1
  N8: IC1.Out_3, SM1.yellow-pin, R2.Pin_1
  N9: IC1.Out_2, SM1.pink-pin, R3.Pin_1
  N10: IC1.Out_1, SM1.blue-pin, R4.Pin_1
  N11: LED1.cathode, R2.Pin_0
  N12: LED2.cathode, R1.Pin_0
  N13: LED3.cathode, R4.Pin_0
  N14: LED4.cathode, R3.Pin_0

custom parts:
  28BYJ-48 Stepper Motor: Unipolar Stepper Motor 28BYJ-48 Top coil - pink & orange Bottom coil - blue & yellow Common rail - red Connector pins: blue - pink - yellow - orange - red
